# Fritzing sketch Prototipo0-BreadBoard (saved by Fritzing 0.8.3b)
breadboards: 1

parts:
  Parte1 = Arduino Fio (Funnel I/O)
  TFT1 = 2.2" TFT with MicroSD Breakout
  S1 = Pushbutton [package="[THT]"]
  S2 = Pushbutton [package="[THT]"]
  S3 = Pushbutton [package="[THT]"]
  S4 = Pushbutton [package="[THT]"]
  J1 = Piezo Speaker
  U1 = LIPO-2000mAh [package=lipo-2000]
  U2 = XBEE-1 [package=xbee-1]
  Parte2 = Thumb Joystick
  U3 = D2523T [package=em406]

nets (from the schematic view):
  VCC: Parte1.VCC, Parte1.AREF, TFT1.BL, TFT1.VIN, U2.VDD, Parte2.SEL, Parte2.VCC, U3.VIN
  GND: Parte1.GND, TFT1.GND, S1.Pin_1, S1.Pin_2, S2.Pin_1, S2.Pin_2, S3.Pin_1, S3.Pin_2, S4.Pin_1, S4.Pin_2, J1.pin2, U1.-, U2.GND, Parte2.GND, U3.GND
  N1: Parte1.D2, U3.TX
  N2: Parte1.D3_PWM, J1.pin1
  N3: Parte1.D5_PWM, S3.Pin_3, S3.Pin_4
  N4: Parte1.D6_PWM, S2.Pin_3, S2.Pin_4
  N5: Parte1.D7, S1.Pin_3, S1.Pin_4
  N6: Parte1.D8, TFT1.RST
  N7: Parte1.D9_PWM, TFT1.SDCS
  N8: Parte1.D10_PWM/SS, TFT1.CS
  N9: Parte1.D11_PWM/MOSI, Parte1.MOSI, TFT1.MOSI
  N10: Parte1.D12/MISO, Parte1.MISO, TFT1.MISO
  N11: Parte1.D13/SCK, Parte1.SCK, TFT1.SCK
  N12: Parte1.VBATT, U1.+
  N13: Parte1.D0/RXI, U2.DOUT
  N14: Parte1.D1/TXO, U2.DIN
  N15: Parte1.A0, Parte2.VERT
  N16: Parte1.A1, Parte2.HORZ
  N17: Parte1.A2, S4.Pin_3, S4.Pin_4

custom parts:
  2.2" TFT with MicroSD Breakout: 2.2" TFT Display with HX8340B Controller and MicroSD Card
